// Logisim project ALU.circ as structural Verilog: 4 circuits, main circuit alu
module alu (
  input  [3:0] A,
  input  [3:0] B,
  input  [1:0] ALUOp,
  output [3:0] C
);

  wire [3:0] and_1_out, n4bit_adder_1_c, or_1_out, sub_1_out_3;

  _4bit_adder u_4bit_adder_1 (.A(A), .B(B), .C(n4bit_adder_1_c));
  sub sub_1 (.in_1(A), .in_2(B), .out_3(sub_1_out_3));
  assign and_1_out = A & B;  // AND_Gate and_1, 4 bits wide
  assign or_1_out = A | B;  // OR_Gate or_1, 4 bits wide
  Multiplexer #(.select(2), .width(4)) multiplexer_1 (
    .in0(n4bit_adder_1_c), .in1(sub_1_out_3), .in2(and_1_out), .in3(or_1_out), .out(C), .sel(ALUOp));  // open: en
endmodule

module _1bit_adder (
  input  a,
  input  b,
  input  cin,
  output overflow,
  output s
);

  wire and_1_out, and_2_out, and_3_out, and_4_out, and_5_out, and_6_out, and_7_out, not_1_out, not_2_out,
       not_3_out, not_4_out, not_5_out, not_6_out;

  and and_1 (and_1_out, b, cin);
  and and_2 (and_2_out, a, cin);
  and and_3 (and_3_out, a, b);
  not not_1 (not_1_out, a);
  not not_2 (not_2_out, b);
  not not_3 (not_3_out, a);
  not not_4 (not_4_out, cin);
  not not_5 (not_5_out, b);
  not not_6 (not_6_out, cin);
  or or_1 (overflow, and_1_out, and_2_out, and_3_out);
  and and_4 (and_4_out, not_1_out, not_2_out, cin);
  and and_5 (and_5_out, not_3_out, b, not_4_out);
  and and_6 (and_6_out, a, not_5_out, not_6_out);
  and and_7 (and_7_out, a, b, cin);
  or or_2 (s, and_4_out, and_5_out, and_6_out, and_7_out);
endmodule

module _4bit_adder (
  input  [3:0] A,
  input  [3:0] B,
  output [3:0] C
);

  wire n1bit_adder_1_overflow, n1bit_adder_2_overflow, n1bit_adder_3_overflow;

  _1bit_adder u_1bit_adder_1 (.a(A[0]), .b(B[0]), .cin(1'b0), .overflow(n1bit_adder_1_overflow), .s(C[0]));
  _1bit_adder u_1bit_adder_2 (
    .a(A[1]), .b(B[1]), .cin(n1bit_adder_1_overflow), .overflow(n1bit_adder_2_overflow), .s(C[1]));
  _1bit_adder u_1bit_adder_3 (
    .a(A[2]), .b(B[2]), .cin(n1bit_adder_2_overflow), .overflow(n1bit_adder_3_overflow), .s(C[2]));
  _1bit_adder u_1bit_adder_4 (.a(A[3]), .b(B[3]), .cin(n1bit_adder_3_overflow), .s(C[3]));  // open: overflow
endmodule

module sub (
  input  [3:0] in_1,
  input  [3:0] in_2,
  output [3:0] out_3
);

  wire [3:0] n4bit_adder_1_c, not_1_out;

  assign not_1_out = ~in_2;  // NOT_Gate not_1, 4 bits wide
  _4bit_adder u_4bit_adder_1 (.A(in_1), .B(not_1_out), .C(n4bit_adder_1_c));
  _4bit_adder u_4bit_adder_2 (.A(n4bit_adder_1_c), .B(4'b0001), .C(out_3));
endmodule
