// Logisim project CRC.circ as structural Verilog: 2 circuits, main circuit CRC
module CRC (
  input  [7:0] A,
  input  [3:0] B,
  output [10:0] out_3
);

  wire [2:0] mod2_1_c, mod2_2_c, mod2_3_c, mod2_4_c, mod2_5_c, mod2_6_c, mod2_7_c;

  mod2 mod2_1 (.a(A[7:4]), .b(B), .c(mod2_1_c));
  mod2 mod2_2 (.a({mod2_1_c, A[3]}), .b(B), .c(mod2_2_c));
  mod2 mod2_3 (.a({mod2_2_c, A[2]}), .b(B), .c(mod2_3_c));
  mod2 mod2_4 (.a({mod2_3_c, A[1]}), .b(B), .c(mod2_4_c));
  mod2 mod2_5 (.a({mod2_4_c, A[0]}), .b(B), .c(mod2_5_c));
  mod2 mod2_6 (.a({mod2_5_c, 1'b0}), .b(B), .c(mod2_6_c));
  mod2 mod2_7 (.a({mod2_6_c, 1'b0}), .b(B), .c(mod2_7_c));
  mod2 mod2_8 (.a({mod2_7_c, 1'b0}), .b(B), .c(out_3[2:0]));

  assign out_3[10:3] = A;
endmodule

module mod2 (
  input  [3:0] a,
  input  [3:0] b,
  output [2:0] c
);

  wire [2:0] xor_1_out;

  xor xor_1 (xor_1_out[0], a[0], b[0]);
  xor xor_2 (xor_1_out[1], a[1], b[1]);
  xor xor_3 (xor_1_out[2], a[2], b[2]);
  Multiplexer #(.width(3)) multiplexer_1 (.in0(a[2:0]), .in1(xor_1_out), .out(c), .sel(a[3]));  // open: en
endmodule
