// Logisim project FSM.circ as structural Verilog: 2 circuits, main circuit fsm
module fsm (
  input  in_1,
  input  [1:0] In,
  output Z
);

  wire and_1_out, clock_1_out, clock_2_out, register_1_q;
  wire [1:0] register_2_q, trans_1_s_prime;

  Register #(.width(1)) register_1 (.D(in_1), .Q(register_1_q), .clk(clock_1_out));  // open: en, clr
  Clock clock_1 (.out(clock_1_out));
  and and_1 (and_1_out, register_1_q, in_1);
  trans trans_1 (.In(In), .S(register_2_q), .S_prime(trans_1_s_prime));
  Clock clock_2 (.out(clock_2_out));
  Register #(.width(2)) register_2 (
    .D(trans_1_s_prime), .Q(register_2_q), .clk(clock_2_out), .clr(and_1_out));  // open: en
  Comparator #(.width(2)) comparator_1 (.a(2'b11), .b(trans_1_s_prime), .eq(Z));  // open: gt, lt
endmodule

module trans (
  input  [1:0] In,
  input  [1:0] S,
  output [1:0] S_prime
);

  wire and_1_out, and_2_out, and_3_out, and_4_out, not_1_out, not_2_out, not_3_out, not_4_out, not_5_out,
       not_6_out, not_7_out;

  not not_1 (not_1_out, In[0]);
  not not_2 (not_2_out, S[1]);
  not not_3 (not_3_out, In[0]);
  not not_4 (not_4_out, S[0]);
  not not_5 (not_5_out, In[0]);
  not not_6 (not_6_out, S[0]);
  not not_7 (not_7_out, In[1]);
  and and_1 (and_1_out, not_1_out, not_2_out, S[0]);
  and and_2 (and_2_out, not_3_out, S[1], not_4_out);
  and and_3 (and_3_out, not_5_out, S[1], not_6_out);
  and and_4 (and_4_out, not_7_out, In[0]);
  or or_1 (S_prime[1], and_1_out, and_2_out);
  or or_2 (S_prime[0], and_3_out, and_4_out);
endmodule
