// Logisim project main.circ as structural Verilog: 7 circuits, main circuit main
module main (
  input  Reset,
  output [31:0] out_2,
  output out_3,
  output [4:0] out_4,
  output [31:0] out_5,
  output out_6,
  output [4:0] out_7,
  output [31:0] out_8
);

  wire ALUSrc, ComResult, EXTOp, JReg, Jump, MemtoReg, nPC_sel, RegDst, RegRa;
  wire [2:0] ALUOp;
  wire [4:0] multiplexer_1_out;
  wire [31:0] adder_1_out, alu_1_c, Beq_sign_ext, dm_1_out, multiplexer_4_out, multiplexer_5_out, PC, rs_data;

  IFU ifu_1 (
    .Reset(Reset), .sign_ext(Beq_sign_ext), .IfBeq(nPC_sel), .ComResult(ComResult), .Address(out_2[25:0]),
    .Jump(Jump), .Reg_data(rs_data), .JReg(JReg), .PC(PC), .Instr(out_2));
  Multiplexer #(.width(5)) multiplexer_1 (
    .in0(out_2[20:16]), .in1(out_2[15:11]), .out(multiplexer_1_out), .sel(RegDst));  // open: en
  Controller controller_1 (
    .OpCode(out_2[31:26]), .Func(out_2[5:0]), .RegDst(RegDst), .ALUSrc(ALUSrc), .MemtoReg(MemtoReg),
    .RegWrite(out_3), .MemWrite(out_6), .nPC_sel(nPC_sel), .EXTOp(EXTOp), .Jump(Jump), .RegRa(RegRa),
    .JReg(JReg), .ALUOp(ALUOp));
  Multiplexer #(.width(5)) multiplexer_2 (
    .in0(multiplexer_1_out), .in1({5{1'b1}}), .out(out_4), .sel(RegRa));  // open: en
  Multiplexer #(.width(32)) multiplexer_3 (
    .in0(multiplexer_4_out), .in1(adder_1_out), .out(out_5), .sel(RegRa));  // open: en
  Adder #(.width(32)) adder_1 (.a(PC), .b(32'h4), .out(adder_1_out));  // open: cin, cout
  GRF grf_1 (
    .busW(out_5), .WE(out_3), .RA(out_2[25:21]), .RB(out_2[20:16]), .RW(out_4), .Reset(Reset),
    .busA(rs_data), .busB(out_8));
  EXT ext_1 (.SignOp(EXTOp), .in(out_2[15:0]), .out(Beq_sign_ext));
  Multiplexer #(.width(32)) multiplexer_4 (
    .in0({alu_1_c[31:7], out_7, alu_1_c[1:0]}), .in1(dm_1_out), .out(multiplexer_4_out), .sel(MemtoReg));  // open: en
  Multiplexer #(.width(32)) multiplexer_5 (
    .in0(out_8), .in1(Beq_sign_ext), .out(multiplexer_5_out), .sel(ALUSrc));  // open: en
  ALU alu_1 (
    .a(rs_data), .b(multiplexer_5_out), .ALUOp(ALUOp), .shamt(out_2[10:6]),
    .c({alu_1_c[31:7], out_7, alu_1_c[1:0]}), .ComResult(ComResult));
  DM dm_1 (.Adr(out_7), .In(out_8), .WE(out_6), .Reset(Reset), .Out(dm_1_out));

  // Other names for the same wires on the sheet: MemAddr[4:0] = out_7; Address[25:0] = out_2[25:0];
  //   Func[5:0] = out_2[5:0]; Immed[15:0] = out_2[15:0]; Instr[31:0] = out_2; shamt[4:0] = out_2[10:6];
  //   rd[4:0] = out_2[15:11]; rt[4:0] = out_2[20:16]; rs[4:0] = out_2[25:21]; MemData[31:0] = out_8; MemWrite = out_6;
  //   OpCode[5:0] = out_2[31:26]; RegAddr[4:0] = out_4; RegData[31:0] = out_5; RegWrite = out_3
endmodule

module ALU (
  input  [31:0] a,
  input  [31:0] b,
  input  [2:0] ALUOp,
  input  [4:0] shamt,
  output [31:0] c,
  output ComResult
);

  wire comparator_1_gt, comparator_2_eq, not_1_out;
  wire [31:0] adder_1_out, and_1_out, or_1_out, shifter_1_out, subtractor_1_out;

  Adder #(.width(32)) adder_1 (.a(a), .b(b), .out(adder_1_out));  // open: cin, cout
  Subtractor #(.width(32)) subtractor_1 (.a(a), .b(b), .out(subtractor_1_out));  // open: bin, bout
  assign or_1_out = a | b;  // OR_Gate or_1, 32 bits wide
  assign and_1_out = a & b;  // AND_Gate and_1, 32 bits wide
  Shifter #(.width(32)) shifter_1 (.in(b), .\dist (shamt), .out(shifter_1_out));
  Comparator #(.width(32)) comparator_1 (.a({32{1'b0}}), .b(a), .gt(comparator_1_gt));  // open: eq, lt
  Comparator #(.width(32)) comparator_2 (.a(a), .b(b), .eq(comparator_2_eq));  // open: gt, lt
  not not_1 (not_1_out, comparator_1_gt);
  Multiplexer #(.select(3), .width(32)) multiplexer_1 (
    .in0(adder_1_out), .in1(subtractor_1_out), .in2(or_1_out), .in3({32{1'b0}}), .in4({b[15:0], {16{1'b0}}}),
    .in5(and_1_out), .in6({32{1'b0}}), .in7(shifter_1_out), .out(c), .sel(ALUOp));  // open: en
  Multiplexer #(.select(3)) multiplexer_2 (
    .in0(1'b0), .in1(1'b0), .in2(1'b0), .in3(comparator_2_eq), .in4(1'b0), .in5(1'b0), .in6(not_1_out),
    .in7(1'b0), .out(ComResult), .sel(ALUOp));  // open: en
endmodule

module DM (
  input  [4:0] Adr,
  input  [31:0] In,
  input  WE,
  input  Reset,
  output [31:0] Out
);

  wire clock_1_out;

  Clock clock_1 (.out(clock_1_out));
  RAM #(.addrWidth(5), .dataWidth(32), .bus("separate")) ram_1 (
    .addr(Adr), .din(In), .data(Out), .str(WE), .clk(clock_1_out), .clr(Reset));  // open: sel, ld
endmodule

module EXT (
  input  SignOp,
  input  [15:0] in,
  output [31:0] out
);

  wire [31:0] bit_extender_1_out, bit_extender_2_out;

  assign bit_extender_1_out = {{16{1'b0}}, in};  // Bit_Extender bit_extender_1
  assign bit_extender_2_out = {{16{in[15]}}, in};  // Bit_Extender bit_extender_2
  Multiplexer #(.width(32)) multiplexer_1 (
    .in0(bit_extender_1_out), .in1(bit_extender_2_out), .out(out), .sel(SignOp));  // open: en
endmodule

module GRF (
  input  [31:0] busW,
  input  WE,
  input  [4:0] RA,
  input  [4:0] RB,
  input  [4:0] RW,
  input  Reset,
  output [31:0] busA,
  output [31:0] busB
);

  wire and_1_out, and_2_out, and_3_out, and_4_out, and_5_out, and_6_out, and_7_out, and_8_out, and_9_out,
       and_10_out, and_11_out, and_12_out, and_13_out, and_14_out, and_15_out, and_16_out, and_17_out,
       and_18_out, and_19_out, and_20_out, and_21_out, and_22_out, and_23_out, and_24_out, and_25_out,
       and_26_out, and_27_out, and_28_out, and_29_out, and_30_out, and_31_out, clock_1_out, decoder_1_out1,
       decoder_1_out2, decoder_1_out3, decoder_1_out4, decoder_1_out5, decoder_1_out6, decoder_1_out7,
       decoder_1_out8, decoder_1_out9, decoder_1_out10, decoder_1_out11, decoder_1_out12, decoder_1_out13,
       decoder_1_out14, decoder_1_out15, decoder_1_out16, decoder_1_out17, decoder_1_out18, decoder_1_out19,
       decoder_1_out20, decoder_1_out21, decoder_1_out22, decoder_1_out23, decoder_1_out24, decoder_1_out25,
       decoder_1_out26, decoder_1_out27, decoder_1_out28, decoder_1_out29, decoder_1_out30, decoder_1_out31;
  wire [31:0] R1, R2, R3, R4, R5, R6, R7, R8, R9, R10, R11, R12, R13, R14, R15, R16, R17, R18, R19, R20, R21,
       R22, R23, R24, R25, R26, R27, R28, R29, R30, R31;

  Decoder #(.select(5)) decoder_1 (
    .out1(decoder_1_out1), .out2(decoder_1_out2), .out3(decoder_1_out3), .out4(decoder_1_out4),
    .out5(decoder_1_out5), .out6(decoder_1_out6), .out7(decoder_1_out7), .out8(decoder_1_out8),
    .out9(decoder_1_out9), .out10(decoder_1_out10), .out11(decoder_1_out11), .out12(decoder_1_out12),
    .out13(decoder_1_out13), .out14(decoder_1_out14), .out15(decoder_1_out15), .out16(decoder_1_out16),
    .out17(decoder_1_out17), .out18(decoder_1_out18), .out19(decoder_1_out19), .out20(decoder_1_out20),
    .out21(decoder_1_out21), .out22(decoder_1_out22), .out23(decoder_1_out23), .out24(decoder_1_out24),
    .out25(decoder_1_out25), .out26(decoder_1_out26), .out27(decoder_1_out27), .out28(decoder_1_out28),
    .out29(decoder_1_out29), .out30(decoder_1_out30), .out31(decoder_1_out31), .sel(RW));  // open: out0, en
  and and_1 (and_1_out, WE, decoder_1_out1);
  and and_2 (and_2_out, WE, decoder_1_out2);
  and and_3 (and_3_out, WE, decoder_1_out3);
  and and_4 (and_4_out, WE, decoder_1_out4);
  and and_5 (and_5_out, WE, decoder_1_out5);
  and and_6 (and_6_out, WE, decoder_1_out6);
  and and_7 (and_7_out, WE, decoder_1_out7);
  and and_8 (and_8_out, WE, decoder_1_out8);
  and and_9 (and_9_out, WE, decoder_1_out9);
  and and_10 (and_10_out, WE, decoder_1_out10);
  and and_11 (and_11_out, WE, decoder_1_out11);
  and and_12 (and_12_out, WE, decoder_1_out12);
  and and_13 (and_13_out, WE, decoder_1_out13);
  and and_14 (and_14_out, WE, decoder_1_out14);
  and and_15 (and_15_out, WE, decoder_1_out15);
  and and_16 (and_16_out, WE, decoder_1_out16);
  and and_17 (and_17_out, WE, decoder_1_out17);
  and and_18 (and_18_out, WE, decoder_1_out18);
  and and_19 (and_19_out, WE, decoder_1_out19);
  and and_20 (and_20_out, WE, decoder_1_out20);
  and and_21 (and_21_out, WE, decoder_1_out21);
  and and_22 (and_22_out, WE, decoder_1_out22);
  and and_23 (and_23_out, WE, decoder_1_out23);
  and and_24 (and_24_out, WE, decoder_1_out24);
  and and_25 (and_25_out, WE, decoder_1_out25);
  and and_26 (and_26_out, WE, decoder_1_out26);
  and and_27 (and_27_out, WE, decoder_1_out27);
  and and_28 (and_28_out, WE, decoder_1_out28);
  and and_29 (and_29_out, WE, decoder_1_out29);
  and and_30 (and_30_out, WE, decoder_1_out30);
  and and_31 (and_31_out, WE, decoder_1_out31);
  Clock clock_1 (.out(clock_1_out));
  Register #(.width(32)) register_1 (.D(busW), .en(and_1_out), .Q(R1), .clk(clock_1_out), .clr(Reset));
  Register #(.width(32)) register_2 (.D(busW), .en(and_2_out), .Q(R2), .clk(clock_1_out), .clr(Reset));
  Register #(.width(32)) register_3 (.D(busW), .en(and_3_out), .Q(R3), .clk(clock_1_out), .clr(Reset));
  Register #(.width(32)) register_4 (.D(busW), .en(and_4_out), .Q(R4), .clk(clock_1_out), .clr(Reset));
  Register #(.width(32)) register_5 (.D(busW), .en(and_5_out), .Q(R5), .clk(clock_1_out), .clr(Reset));
  Register #(.width(32)) register_6 (.D(busW), .en(and_6_out), .Q(R6), .clk(clock_1_out), .clr(Reset));
  Register #(.width(32)) register_7 (.D(busW), .en(and_7_out), .Q(R7), .clk(clock_1_out), .clr(Reset));
  Register #(.width(32)) register_8 (.D(busW), .en(and_8_out), .Q(R8), .clk(clock_1_out), .clr(Reset));
  Register #(.width(32)) register_9 (.D(busW), .en(and_9_out), .Q(R9), .clk(clock_1_out), .clr(Reset));
  Register #(.width(32)) register_10 (.D(busW), .en(and_10_out), .Q(R10), .clk(clock_1_out), .clr(Reset));
  Register #(.width(32)) register_11 (.D(busW), .en(and_11_out), .Q(R11), .clk(clock_1_out), .clr(Reset));
  Register #(.width(32)) register_12 (.D(busW), .en(and_12_out), .Q(R12), .clk(clock_1_out), .clr(Reset));
  Register #(.width(32)) register_13 (.D(busW), .en(and_13_out), .Q(R13), .clk(clock_1_out), .clr(Reset));
  Register #(.width(32)) register_14 (.D(busW), .en(and_14_out), .Q(R14), .clk(clock_1_out), .clr(Reset));
  Register #(.width(32)) register_15 (.D(busW), .en(and_15_out), .Q(R15), .clk(clock_1_out), .clr(Reset));
  Register #(.width(32)) register_16 (.D(busW), .en(and_16_out), .Q(R16), .clk(clock_1_out), .clr(Reset));
  Register #(.width(32)) register_17 (.D(busW), .en(and_17_out), .Q(R17), .clk(clock_1_out), .clr(Reset));
  Register #(.width(32)) register_18 (.D(busW), .en(and_18_out), .Q(R18), .clk(clock_1_out), .clr(Reset));
  Register #(.width(32)) register_19 (.D(busW), .en(and_19_out), .Q(R19), .clk(clock_1_out), .clr(Reset));
  Register #(.width(32)) register_20 (.D(busW), .en(and_20_out), .Q(R20), .clk(clock_1_out), .clr(Reset));
  Register #(.width(32)) register_21 (.D(busW), .en(and_21_out), .Q(R21), .clk(clock_1_out), .clr(Reset));
  Register #(.width(32)) register_22 (.D(busW), .en(and_22_out), .Q(R22), .clk(clock_1_out), .clr(Reset));
  Register #(.width(32)) register_23 (.D(busW), .en(and_23_out), .Q(R23), .clk(clock_1_out), .clr(Reset));
  Register #(.width(32)) register_24 (.D(busW), .en(and_24_out), .Q(R24), .clk(clock_1_out), .clr(Reset));
  Register #(.width(32)) register_25 (.D(busW), .en(and_25_out), .Q(R25), .clk(clock_1_out), .clr(Reset));
  Register #(.width(32)) register_26 (.D(busW), .en(and_26_out), .Q(R26), .clk(clock_1_out), .clr(Reset));
  Register #(.width(32)) register_27 (.D(busW), .en(and_27_out), .Q(R27), .clk(clock_1_out), .clr(Reset));
  Register #(.width(32)) register_28 (.D(busW), .en(and_28_out), .Q(R28), .clk(clock_1_out), .clr(Reset));
  Register #(.width(32)) register_29 (.D(busW), .en(and_29_out), .Q(R29), .clk(clock_1_out), .clr(Reset));
  Register #(.width(32)) register_30 (.D(busW), .en(and_30_out), .Q(R30), .clk(clock_1_out), .clr(Reset));
  Register #(.width(32)) register_31 (.D(busW), .en(and_31_out), .Q(R31), .clk(clock_1_out), .clr(Reset));
  Multiplexer #(.select(5), .width(32)) multiplexer_1 (
    .in0({32{1'b0}}), .in1(R1), .in2(R2), .in3(R3), .in4(R4), .in5(R5), .in6(R6), .in7(R7), .in8(R8),
    .in9(R9), .in10(R10), .in11(R11), .in12(R12), .in13(R13), .in14(R14), .in15(R15), .in16(R16), .in17(R17),
    .in18(R18), .in19(R19), .in20(R20), .in21(R21), .in22(R22), .in23(R23), .in24(R24), .in25(R25),
    .in26(R26), .in27(R27), .in28(R28), .in29(R29), .in30(R30), .in31(R31), .out(busA), .sel(RA));  // open: en
  Multiplexer #(.select(5), .width(32)) multiplexer_2 (
    .in0({32{1'b0}}), .in1(R1), .in2(R2), .in3(R3), .in4(R4), .in5(R5), .in6(R6), .in7(R7), .in8(R8),
    .in9(R9), .in10(R10), .in11(R11), .in12(R12), .in13(R13), .in14(R14), .in15(R15), .in16(R16), .in17(R17),
    .in18(R18), .in19(R19), .in20(R20), .in21(R21), .in22(R22), .in23(R23), .in24(R24), .in25(R25),
    .in26(R26), .in27(R27), .in28(R28), .in29(R29), .in30(R30), .in31(R31), .out(busB), .sel(RB));  // open: en
endmodule

module IFU (
  input  Reset,
  input  [31:0] sign_ext,
  input  IfBeq,
  input  ComResult,
  input  [25:0] Address,
  input  Jump,
  input  [31:0] Reg_data,
  input  JReg,
  output [31:0] PC,
  output [31:0] Instr
);

  wire and_1_out, clock_1_out;
  wire [31:0] adder_1_out, adder_2_out, multiplexer_1_out, multiplexer_2_out, multiplexer_3_out;

  Register #(.width(32)) u_PC (.D(multiplexer_3_out), .Q(PC), .clk(clock_1_out), .clr(Reset));  // open: en
  Clock clock_1 (.out(clock_1_out));
  and and_1 (and_1_out, IfBeq, ComResult);
  Adder #(.width(32)) adder_1 (.a(PC), .b(32'h4), .out(adder_1_out));  // open: cin, cout
  Adder #(.width(32)) adder_2 (.a(adder_1_out), .b({sign_ext[29:0], 2'b00}), .out(adder_2_out));  // open: cin, cout
  ROM #(.addrWidth(5), .dataWidth(32)) rom_1 (.addr(PC[6:2]), .data(Instr));  // open: sel
  Multiplexer #(.width(32)) multiplexer_1 (
    .in0(adder_1_out), .in1(adder_2_out), .out(multiplexer_1_out), .sel(and_1_out));  // open: en
  Multiplexer #(.width(32)) multiplexer_2 (
    .in0(multiplexer_1_out), .in1({PC[31:28], Address, 2'b00}), .out(multiplexer_2_out), .sel(Jump));  // open: en
  Multiplexer #(.width(32)) multiplexer_3 (
    .in0(multiplexer_2_out), .in1(Reg_data), .out(multiplexer_3_out), .sel(JReg));  // open: en

  // Notes on the sheet:
  //   contents of rom_1 (hex, n*v repeats v):
  //   34040012 42140 ad040000 423c0 ad040004 42280 ad040008
endmodule

module Controller (
  input  [5:0] OpCode,
  input  [5:0] Func,
  output Jump,
  output RegDst,
  output ALUSrc,
  output MemtoReg,
  output MemWrite,
  output nPC_sel,
  output EXTOp,
  output RegRa,
  output JReg,
  output [2:0] ALUOp,
  output RegWrite
);

  wire addu1_out, addu2, addu_out, and1_out, and2, and_out, beq_out, bgez_out, j_out, jal_out, jr1_out, jr2,
       jr_out, lui_out, lw_out, not_1_out, not_2_out, not_3_out, not_4_out, not_5_out, not_6_out, not_7_out,
       not_8_out, not_9_out, not_10_out, not_11_out, not_12_out, ori_out, sll1_out, sll2, sll_out, subu1_out,
       subu2, subu_out, sw_out;

  not not_1 (not_1_out, OpCode[5]);
  not not_2 (not_2_out, OpCode[4]);
  not not_3 (not_3_out, Func[5]);
  not not_4 (not_4_out, OpCode[3]);
  not not_5 (not_5_out, Func[4]);
  not not_6 (not_6_out, OpCode[2]);
  not not_7 (not_7_out, Func[3]);
  not not_8 (not_8_out, OpCode[1]);
  not not_9 (not_9_out, Func[2]);
  not not_10 (not_10_out, OpCode[0]);
  not not_11 (not_11_out, Func[1]);
  and addu1 (addu1_out, not_1_out, not_2_out, not_4_out, not_6_out, not_8_out, not_10_out);
  and subu1 (subu1_out, not_1_out, not_2_out, not_4_out, not_6_out, not_8_out, not_10_out);
  and ori (ori_out, not_1_out, not_2_out, OpCode[3], OpCode[2], not_8_out, OpCode[0]);
  and lw (lw_out, OpCode[5], not_2_out, not_4_out, not_6_out, OpCode[1], OpCode[0]);
  and sw (sw_out, OpCode[5], not_2_out, OpCode[3], not_6_out, OpCode[1], OpCode[0]);
  and beq (beq_out, not_1_out, not_2_out, not_4_out, OpCode[2], not_8_out, not_10_out);
  and lui (lui_out, not_1_out, not_2_out, OpCode[3], OpCode[2], OpCode[1], OpCode[0]);
  and j (j_out, not_1_out, not_2_out, not_4_out, not_6_out, OpCode[1], not_10_out);
  and jal (jal_out, not_1_out, not_2_out, not_4_out, not_6_out, OpCode[1], OpCode[0]);
  and jr1 (jr1_out, not_1_out, not_2_out, not_4_out, not_6_out, not_8_out, not_10_out);
  and and1 (and1_out, not_1_out, not_2_out, not_4_out, not_6_out, not_8_out, not_10_out);
  and bgez (bgez_out, not_1_out, not_2_out, not_4_out, not_6_out, not_8_out, OpCode[0]);
  and sll1 (sll1_out, not_1_out, not_2_out, not_4_out, not_6_out, not_8_out, not_10_out);
  not not_12 (not_12_out, Func[0]);
  and \and  (and_out, and2, and1_out);
  and sll (sll_out, sll2, sll1_out);
  and u_addu2 (addu2, Func[5], not_5_out, not_7_out, not_9_out, not_11_out, Func[0]);
  and u_subu2 (subu2, Func[5], not_5_out, not_7_out, not_9_out, Func[1], Func[0]);
  and u_jr2 (jr2, not_3_out, not_5_out, Func[3], not_9_out, not_11_out, not_12_out);
  and u_and2 (and2, Func[5], not_5_out, not_7_out, Func[2], not_11_out, not_12_out);
  and u_sll2 (sll2, not_3_out, not_5_out, not_7_out, not_9_out, not_11_out, not_12_out);
  and addu (addu_out, addu2, addu1_out);
  and subu (subu_out, subu2, subu1_out);
  and jr (jr_out, jr2, jr1_out);
  or u_RegDst (RegDst, sll_out, addu_out, subu_out, and_out);
  or u_ALUSrc (ALUSrc, ori_out, lw_out, sw_out, lui_out);
  buf u_MemtoReg (MemtoReg, lw_out);  // OR_Gate
  or u_RegWrite (RegWrite, sll_out, and_out, addu_out, subu_out, ori_out, lw_out, lui_out, jal_out);
  buf u_MemWrite (MemWrite, sw_out);  // OR_Gate
  or u_nPC_sel (nPC_sel, beq_out, bgez_out);
  or u_EXTOp (EXTOp, lw_out, bgez_out, sw_out, beq_out);
  or ALUOp2 (ALUOp[2], and_out, sll_out, lui_out, bgez_out);
  or ALUOp1 (ALUOp[1], bgez_out, ori_out, sll_out, beq_out);
  or ALUOp0 (ALUOp[0], and_out, subu_out, sll_out, beq_out);
  or u_Jump (Jump, j_out, jal_out);
  buf u_RegRa (RegRa, jal_out);  // OR_Gate
  buf u_JReg (JReg, jr_out);  // OR_Gate
endmodule
